# Fritzing sketch controller (saved by Fritzing 0.8.7b)
breadboards: 1

parts:
  Part1 = Arduino Uno (Rev3)
  LED2 = LED - 5mm [color="Red (633nm)" package="5 mm [THT]"]
  LED3 = smd LED [color="Green (570nm)" package="1206 [SMD]"]
  R1 = Resistor [tolerance=±5% resistance=220 package=THT]
  R2 = Resistor [tolerance=±5% resistance=220 package=THT]
  U1 = XBee
  R3 = Resistor [tolerance=±5% resistance=220 package=THT]
  R4 = Resistor [tolerance=±5% resistance=220 package=THT]
  LED4 = LED - 5mm [color="Red (633nm)" package="5 mm [THT]"]
  LED5 = LED - 5mm [color="Green (570nm)" package="5 mm [THT]"]

nets:
  N1: Part1.D9_PWM, LED4.cathode
  N2: Part1.D10_PWM/SS, LED5.cathode
  N3: Part1.D11_PWM/MOSI, LED2.cathode
  N4: Part1.D12/MISO, LED3.cathode
  GND: Part1.GND, R1.Pin_1, R2.Pin_1, U1.GND, R3.Pin_1, R4.Pin_1
  N5: Part1.D0/RX, U1.pin20
  N6: Part1.D1/TX, U1.pin19
  3V3: Part1.3V3, U1.VCC
  N7: LED2.anode, R1.Pin_0
  N8: LED3.anode, R2.Pin_0
  N9: R3.Pin_0, LED5.anode
  N10: R4.Pin_0, LED4.anode
