# Fritzing sketch sensor (saved by Fritzing 0.8.7b)
breadboards: 1

parts:
  Part1 = Arduino Uno (Rev3)
  R1 = Photocell (LDR) [package=THT]
  PIR1 = PIR sensor
  R2 = Resistor [tolerance=±5% resistance=220 package=THT]

nets:
  N1: Part1.D2, R1.pin_1, R2.Pin_0
  N2: Part1.D3_PWM, PIR1.SIG
  5V: Part1.5V, R1.pin_0, PIR1.VDD
  GND: Part1.GND, PIR1.GND, R2.Pin_1
